// Logisim project scheme.circ as structural Verilog: 1 circuit, main circuit main
module main (
  input  x2,
  input  x1,
  input  x0,
  input  clk,
  output y1,
  output y0
);

  wire and_1_out, and_2_out, and_3_out, and_4_out, and_5_out, and_6_out, and_7_out, and_8_out, and_9_out,
       and_10_out, and_11_out, and_12_out, and_13_out, and_14_out, and_15_out, and_16_out, and_17_out,
       and_18_out, not_1_out, not_2_out, not_3_out, or_3_out, or_4_out, Q0_q, Q0_qn, Q1_q, Q1_qn, Q2_q,
       Q2_qn, R_out, S_out;

  not not_1 (not_1_out, x2);
  not not_2 (not_2_out, x1);
  not not_3 (not_3_out, x0);
  and and_1 (and_1_out, not_1_out, Q1_q);
  and and_2 (and_2_out, not_2_out, x0, Q1_q);
  and and_3 (and_3_out, not_1_out, x1, x0);
  and and_4 (and_4_out, not_1_out, x1, Q2_q);
  and and_5 (and_5_out, not_1_out, x1, x0, Q1_qn);
  and and_6 (and_6_out, not_1_out, x0, Q1_qn, Q0_q);
  and and_7 (and_7_out, not_1_out, not_2_out, not_3_out, Q1_qn, Q0_qn);
  and S (S_out, x2, x1, x0);
  and R (R_out, x2, x1, not_3_out);
  and and_8 (and_8_out, Q1_q, Q0_qn);
  and and_9 (and_9_out, x1, not_3_out, Q2_q, Q1_q);
  and and_10 (and_10_out, x2, x1, Q1_q);
  and and_11 (and_11_out, x2, not_2_out, not_3_out);
  and and_12 (and_12_out, not_1_out, not_2_out, not_3_out, Q0_qn);
  and and_13 (and_13_out, not_1_out, not_2_out, x0, Q0_q);
  and and_14 (and_14_out, x2, not_2_out, not_3_out, Q0_q);
  and and_15 (and_15_out, not_2_out, x0, Q1_q);
  and and_16 (and_16_out, not_1_out, Q2_qn, Q1_q);
  and and_17 (and_17_out, not_1_out, not_2_out, Q1_q);
  and and_18 (and_18_out, not_1_out, x0, Q1_q);
  or or_1 (y1, and_1_out, and_2_out, and_3_out, and_4_out);
  or or_2 (y0, and_5_out, and_6_out, and_7_out);
  or or_3 (or_3_out, and_8_out, and_9_out, and_10_out, and_11_out);
  or or_4 (or_4_out, and_12_out, and_13_out, and_14_out, and_15_out, and_16_out, and_17_out, and_18_out);
  S_R_Flip_Flop Q2 (.S(S_out), .clk(clk), .R(R_out), .Q(Q2_q), .Qn(Q2_qn));  // open: preset, reset, en
  D_Flip_Flop Q1 (.clk(clk), .D(or_3_out), .Q(Q1_q), .Qn(Q1_qn));  // open: preset, en, reset
  T_Flip_Flop Q0 (.clk(clk), .T(or_4_out), .Q(Q0_q), .Qn(Q0_qn));  // open: preset, reset, en
endmodule
